# Fritzing sketch Electrical design (saved by Fritzing 0.9.3b)
breadboards: 2

parts:
  U1 = ESP8266 NodeMCU LoLin module
  M1 = DC Motor
  M2 = DC Motor
  M3 = DC Motor
  M4 = DC Motor
  IC1 = L293D [package=THT]
  IC2 = L293D [package=THT]
  VCC1 = Battery
  S1 = Round Pushbutton
  Part1 = SRF05 Ultrasonic Rangefinder
  M5 = fc-51 [package=THT]
  M6 = fc-51 [part_number=RightIr package=THT]
  S2 = Reed switch [package=THT]
  R1 = Resistor [tolerance=±5% resistance=10k package=THT]

nets:
  N1: U1.D0, IC1.In_4, IC2.In_1
  N2: U1.D1, M1.pin_2, IC1.In_3, IC2.In_2
  N3: U1.D2, IC1.In_1, IC2.In_4
  N4: U1.D3, M2.pin_2, IC1.In_2, IC2.In_3
  N5: U1.D4, Part1.Echo
  GND: U1.GND, IC1.0V, IC2.0V, VCC1.-, S1.leg0, S1.leg1, Part1.GND, M5.pin2, M6.pin2, R1.Pin_0
  N6: U1.D5, M6.pin1
  N7: U1.D6, M5.pin1
  N8: U1.D7, Part1.Trig
  N9: U1.D8, S2.pin_1, R1.Pin_1
  N10: M1.pin_1, IC1.Out_4_(_Controlled_by_Enable_2_)
  N11: M2.pin_1, IC1.Out_1_(_Controlled_by_Enable_1_)
  N12: M3.pin_1, IC2.Out_1_(_Controlled_by_Enable_1_)
  N13: M3.pin_2, IC2.Out_2_(_Controlled_by_Enable_1_)
  N14: M4.pin_1, IC2.Out_4_(_Controlled_by_Enable_2_)
  N15: M4.pin_2, IC2.Out_3_(_Controlled_by_Enable_2_)
  N16: IC1.Enable_1, IC1.+Vmotor, IC1.Enable_2, IC1.+V, IC2.Enable_1, IC2.+Vmotor, IC2.Enable_2, IC2.+V, VCC1.+, Part1.VCC, M5.pin3, M6.pin3, S2.pin_2

notes:
  Right IR
  left IR
  Reset button
  5V power supply
  Front left motor
  Rear left motor
  Front right motor
  Rear right motor
  Ultra sonic sensor
  Reed switch

custom parts:
  ESP8266 NodeMCU LoLin module: ESP8266 based NodeMCU
